// Logisim project X64000.circ as structural Verilog: 9 circuits, main circuit MemCell
module MemCell (
  input  A,
  output Q
);

  wire and_1_out, d_ff_1_qn, not_1_out, undriven, undriven_2;

  and and_1 (and_1_out, 1'b1, A);
  // NoConnect on undriven
  // NoConnect on undriven_2
  D_Flip_Flop d_ff_1 (.D(undriven), .clk(undriven_2), .Q(Q), .Qn(d_ff_1_qn), .preset(and_1_out), .reset(not_1_out));
  // NoConnect on d_ff_1_qn
  not not_1 (not_1_out, A);
endmodule

module MemGrid4 (
  input  [3:0] in_1,
  output A0,
  output A1,
  output A2,
  output A3
);

  MemCell memcell_1 (.A(in_1[0]), .Q(A0));
  MemCell memcell_2 (.A(in_1[1]), .Q(A1));
  MemCell memcell_3 (.A(in_1[2]), .Q(A2));
  MemCell memcell_4 (.A(in_1[3]), .Q(A3));
endmodule

module Bank8 (
  input  [7:0] in_1,
  output [7:0] out_2
);

  MemGrid4 memgrid4_1 (.in_1(in_1[3:0]), .A0(out_2[0]), .A1(out_2[1]), .A2(out_2[2]), .A3(out_2[3]));
  MemGrid4 memgrid4_2 (.in_1(in_1[7:4]), .A0(out_2[4]), .A1(out_2[5]), .A2(out_2[6]), .A3(out_2[7]));
endmodule

module Memory64 (
  input  [63:0] in_1,
  output [63:0] out_2
);

  Bank8 bank8_1 (.in_1(in_1[7:0]), .out_2(out_2[7:0]));
  Bank8 bank8_2 (.in_1(in_1[15:8]), .out_2(out_2[15:8]));
  Bank8 bank8_3 (.in_1(in_1[23:16]), .out_2(out_2[23:16]));
  Bank8 bank8_4 (.in_1(in_1[31:24]), .out_2(out_2[31:24]));
  Bank8 bank8_5 (.in_1(in_1[39:32]), .out_2(out_2[39:32]));
  Bank8 bank8_6 (.in_1(in_1[47:40]), .out_2(out_2[47:40]));
  Bank8 bank8_7 (.in_1(in_1[55:48]), .out_2(out_2[55:48]));
  Bank8 bank8_8 (.in_1(in_1[63:56]), .out_2(out_2[63:56]));
endmodule

module CanWrite (
  input  WRITE,
  output ENABLED
);

  wire memcell_1_q;

  MemCell memcell_1 (.A(WRITE), .Q(memcell_1_q));
  and and_1 (ENABLED, memcell_1_q, 1'b1);
endmodule

module Register64 (
  input  [63:0] Reg64In,
  output [63:0] Reg64Out
);

  Memory64 memory64_1 (.in_1(Reg64In), .out_2(Reg64Out));
endmodule

module ProgramCounterInc64 (
  input  [63:0] BaseProgramAddress,
  input  [63:0] JumpTo,
  output [63:0] DestProgramAddress,
  output Overflow
);

  Adder #(.width(64)) adder_1 (
    .a(BaseProgramAddress), .b(JumpTo), .out(DestProgramAddress), .cout(Overflow));  // open: cin
endmodule

module ProgramCounter64 (
  input  [63:0] ProgramCnterIn,
  output [63:0] Result,
  output Overflow
);

  ProgramCounterInc64 programcounterinc64_1 (
    .BaseProgramAddress(ProgramCnterIn), .JumpTo(64'h8), .DestProgramAddress(Result), .Overflow(Overflow));
endmodule

module MainCircuit (
  output [63:0] ProgramCounterOut
);

  wire and_1_out, ClockIn_out, not_1_out, programcounter64_1_overflow;
  wire [63:0] ram_1_dout, register64_1_reg64out;

  RAM #(.dataWidth(64)) ram_1 (
    .addr(ProgramCounterOut[7:0]), .we(and_1_out), .oe(and_1_out), .clk(and_1_out), .din(ProgramCounterOut),
    .dout(ram_1_dout));
  ProgramCounter64 programcounter64_1 (
    .ProgramCnterIn(register64_1_reg64out), .Result(ProgramCounterOut), .Overflow(programcounter64_1_overflow));
  Clock #(.phaseOffset(1)) ClockIn (.out(ClockIn_out));
  not not_1 (not_1_out, programcounter64_1_overflow);
  and and_1 (and_1_out, ClockIn_out, not_1_out);
  Register64 register64_1 (.Reg64In(ram_1_dout), .Reg64Out(register64_1_reg64out));
endmodule
